// Logisim project P2.circ as structural Verilog
module Execute (
  input  [31:0] ReadD1,
  input  [31:0] ReadD2,
  input  [31:0] FromImmGen,
  input  WriteRegisterInstructionInput,
  input  ControlExecuteMux,
  input  [3:0] ControlOpCode,
  input  [4:0] ControlShiftAmount,
  input  Clock
);

  wire [7:1] undriven;
  wire [31:0] alu_1_p5, multiplexer_1_out;

  Multiplexer #(.width(32), .enable("false")) multiplexer_1 (
    .in0(ReadD2), .in1(FromImmGen), .out(multiplexer_1_out), .sel(ControlExecuteMux));
  // ALU alu_1: pin names not known; wires that end beside it: ReadD1, multiplexer_1_out, ControlOpCode, ControlShiftAmount, alu_1_p5
  Register #(.width(32)) Result (.D(alu_1_p5), .clk(Clock));  // open: en, Q, clr
  Register #(.width(32)) ReadData2 (.D(ReadD2), .clk(Clock));  // open: en, Q, clr
  Register WriteRegisterInstruction (.D({undriven, WriteRegisterInstructionInput}), .clk(Clock));  // open: en, Q, clr
  // Pins of 1 and 8 bits meet at {undriven, WriteRegisterInstructionInput}
endmodule

module Decode (
  input  Instruction,
  input  Clock
);

  wire immgen_1_out_2;
  wire [7:0] control_1_p2, control_1_p3, control_1_p4, control_1_p5, control_1_p6, control_1_p7,
       control_1_p8, registerfile_1_p2, registerfile_1_p3, undriven;

  // Control control_1: pin names not known; wires that end beside it: Instruction, control_1_p2, control_1_p3, control_1_p4, control_1_p5, control_1_p6, control_1_p7, control_1_p8
  // RegisterFile registerfile_1: pin names not known; wires that end beside it: control_1_p7, registerfile_1_p2, registerfile_1_p3
  ImmGen immgen_1 (.out_2(immgen_1_out_2));  // open: in_1
  Register WB1 (.D(control_1_p2), .clk(Clock));  // open: en, Q, clr
  Register M1 (.D(control_1_p4), .clk(Clock));  // open: en, Q, clr
  Register EX1 (.D(control_1_p7), .clk(Clock));  // open: en, Q, clr
  Register ReadD1 (.D(registerfile_1_p2), .clk(Clock));  // open: en, Q, clr
  Register FromImmGen ();  // open: D, en, Q, clk, clr
  Register WriteRegisterInstruction (.D(undriven), .clk(Clock));  // open: en, Q, clr
  Register WB2 (.D(control_1_p3), .clk(Clock));  // open: en, Q, clr
  Register M2 (.D(control_1_p5), .clk(Clock));  // open: en, Q, clr
  Register EX2 (.D(control_1_p8), .clk(Clock));  // open: en, Q, clr
  Register ReadD2 (.D(registerfile_1_p3), .clk(Clock));  // open: en, Q, clr
  Register M3 (.D(control_1_p6), .clk(Clock));  // open: en, Q, clr
endmodule

module Control (
  input  Instruction,
  output WB1,
  output WB2,
  output M1,
  output M2,
  output M3,
  output EX1,
  output EX2
);


  // Notes on the sheet:
  //   Control
endmodule

module ImmGen (
  input  in_1,
  output out_2
);


  assign out_2 = in_1;

  // Notes on the sheet:
  //   Imm Gen
endmodule

module Fetch (
  input  Clock
);

  wire risc_vprogramrom_1_p3;
  wire [31:0] counter_1_q, risc_vprogramrom_1_p2, risc_vprogramrom_1_p4;

  Counter #(.width(32), .max('hffffffff)) counter_1 (.Q(counter_1_q));  // open: clr, load, up, count, clk, D, carry
  // Incrementer incrementer_1: pin names not known; wires that end beside it: counter_1_q, counter_1_q
  // RISC_VProgramROM risc_vprogramrom_1: pin names not known; wires that end beside it: Clock, risc_vprogramrom_1_p2, risc_vprogramrom_1_p3, risc_vprogramrom_1_p4
  Register #(.width(32)) register_1 (
    .D(risc_vprogramrom_1_p2), .clk(risc_vprogramrom_1_p3), .Q(risc_vprogramrom_1_p4));  // open: en, clr
endmodule
